// Logisim project Circuito contador Gray 4 bits.circ as structural Verilog: 1 circuit, main circuit ContadorGray
module ContadorGray (
);

  wire and_1_out, and_2_out, and_3_out, and_4_out, and_5_out, and_6_out, and_7_out, and_8_out, and_9_out,
       and_10_out, and_11_out, and_12_out, and_13_out, and_14_out, and_15_out, and_16_out, clock_1_out,
       or_1_out, or_2_out, or_3_out, or_4_out, Q0D_q, Q0D_qn, Q1C_q, Q1C_qn, Q2B_q, Q2B_qn, Q3A_q, Q3A_qn;

  Clock clock_1 (.out(clock_1_out));
  J_K_Flip_Flop Q0D (.J(or_4_out), .K(or_3_out), .clk(clock_1_out), .Q(Q0D_q), .Qn(Q0D_qn));  // open: preset, reset
  J_K_Flip_Flop Q1C (.J(or_2_out), .K(or_1_out), .clk(clock_1_out), .Q(Q1C_q), .Qn(Q1C_qn));  // open: preset, reset
  J_K_Flip_Flop Q2B (.J(and_4_out), .K(and_3_out), .clk(clock_1_out), .Q(Q2B_q), .Qn(Q2B_qn));  // open: preset, reset
  J_K_Flip_Flop Q3A (.J(and_2_out), .K(and_1_out), .clk(clock_1_out), .Q(Q3A_q), .Qn(Q3A_qn));  // open: preset, reset
  and and_1 (and_1_out, Q1C_qn, Q0D_qn, Q2B_qn);
  and and_2 (and_2_out, Q0D_qn, Q2B_q, Q1C_qn);
  and and_3 (and_3_out, Q0D_qn, Q1C_q, Q3A_q);
  and and_4 (and_4_out, Q1C_q, Q0D_qn, Q3A_qn);
  and and_5 (and_5_out, Q3A_qn, Q2B_q, Q0D_q);
  and and_6 (and_6_out, Q0D_q, Q2B_qn, Q3A_q);
  and and_7 (and_7_out, Q0D_q, Q2B_q, Q3A_q);
  and and_8 (and_8_out, Q0D_q, Q2B_qn, Q3A_qn);
  and and_9 (and_9_out, Q3A_qn, Q1C_qn, Q2B_q);
  and and_10 (and_10_out, Q3A_qn, Q1C_q, Q2B_qn);
  and and_11 (and_11_out, Q3A_q, Q1C_qn, Q2B_qn);
  and and_12 (and_12_out, Q3A_q, Q1C_q, Q2B_q);
  and and_13 (and_13_out, Q3A_qn, Q1C_qn, Q2B_qn);
  and and_14 (and_14_out, Q3A_qn, Q1C_q, Q2B_q);
  and and_15 (and_15_out, Q3A_q, Q1C_qn, Q2B_q);
  and and_16 (and_16_out, Q3A_q, Q1C_q, Q2B_qn);
  or or_1 (or_1_out, and_5_out, and_6_out);
  or or_2 (or_2_out, and_7_out, and_8_out);
  or or_3 (or_3_out, and_9_out, and_10_out, and_11_out, and_12_out);
  or or_4 (or_4_out, and_13_out, and_14_out, and_15_out, and_16_out);
endmodule
