// Digital circuit Barramento Digital.dig as structural Verilog
module Barramento_Digital (
  input  in_1,
  input  in_2,
  input  in_3,
  input  clk,
  input  in_5
);

  wire dipswitch_1_out;
  wire [3:0] u_controlador_aut;

  DipSwitch dipswitch_1 (.out(dipswitch_1_out));
  controlador #(.applicationType("GHDL")) u_controlador (
    .req({in_5, in_3, in_2, in_1}), .reset(dipswitch_1_out), .clock(clk), .aut(u_controlador_aut));
  LED led_1 (.in(u_controlador_aut[0]));
  LED led_2 (.in(u_controlador_aut[1]));
  LED led_3 (.in(u_controlador_aut[2]));
  LED led_4 (.in(u_controlador_aut[3]));
endmodule

/* Code of controlador:
library ieee;
use ieee.std_logic_1164.all;
entity controlador is
    port (
    req : in std_logic_vector (3 downto 0);
    aut : out std_logic_vector (3 downto 0);
    reset : in std_logic;
    clock : in std_logic
    );
end entity controlador;
architecture comport_controlador of controlador is
    TYPE Tipo_estado IS (inicio, zero, um, dois, tres);
    signal atual: Tipo_estado;
    begin
        process(clock, reset)
        begin
            if reset = '1' then
                atual <= inicio;
            elsif (clock'event and clock = '1') then
                case atual is
                    when inicio =>
                        if(req(0)='1') then
                            atual <= zero;
                        elsif (req(1)='1') then
                            atual <= um;
                        elsif (req(2)='1') then
                            atual <= dois;
                        elsif (req(3)='1') then
                            atual <= tres;
                        end if;
                    when zero =>
                        if(req(0)='0') then 
                            atual<= inicio;
                        end if;
                    when um =>
                        if(req(1)='0') then 
                            atual<= inicio;
                        end if;
                    when dois =>
                        if(req(2)='0') then 
                            atual<= inicio;
                        end if;
                    when tres =>
                        if(req(3)='0') then 
                            atual<= inicio;
                        end if;
                end case;
            end if;
        end process;
        process(atual)
        begin
            case atual is
                when inicio =>
                    aut <="0000";
                when zero =>
                    aut(0)<='1';
                when um =>
                    aut(1)<='1';
                when dois =>
                    aut(2)<='1';
                when tres =>
                    aut(3)<='1';
                when others =>
                    aut <="0000";
            end case;
        end process;
end comport_controlador;
*/
